# Fritzing sketch fritzing (saved by Fritzing 0.6.3b)
breadboards: 1

parts:
  Q1 = NPN-Transistor [package="TO92 [THT]"]  # not connected
  R1 = Resistor [tolerance=±5% resistance=220 package=THT]  # not connected
  R2 = Resistor [tolerance=±5% resistance=220 package=THT]  # not connected
  Arduino1 = Arduino
  LED1 = RGB LED (com. cathode, rbg) [package="5 mm [THT]"]
  LED2 = RGB LED (com. cathode, rbg) [package="5 mm [THT]"]
  C1 = Electrolytic Capacitor [capacitance=1µF package="100 mil [THT, electrolytic]"]
  R3 = Trimmer Potentiometer [maximum_resistance=10kΩ package=THT]
  R4 = Resistor [tolerance=±5% resistance=220 package=THT]
  R5 = Resistor [tolerance=±5% resistance=220 package=THT]
  LED3 = RGB LED (com. cathode, rbg) [package="5 mm [THT]"]
  R6 = Resistor [tolerance=±5% resistance=220 package=THT]
  R7 = Resistor [tolerance=±5% resistance=220 package=THT]
  R8 = Resistor [tolerance=±5% resistance=220 package=THT]
  R9 = Resistor [tolerance=±5% resistance=220 package=THT]
  MIC1 = Microphone
  R10 = Resistor [tolerance=±5% resistance=220 package=THT]
  R11 = Resistor [tolerance=±5% resistance=220 package=THT]
  LED4 = RGB LED (com. cathode, rbg) [package="5 mm [THT]"]
  IC1 = IC, DIP package, 8 pins [chip_label=ON spacing=300mil]

nets:
  N1: Arduino1.D9, R11.Pin_0
  N2: Arduino1.D8, R10.Pin_0
  N3: Arduino1.D7, R9.Pin_0
  N4: Arduino1.D6, R8.Pin_0
  N5: Arduino1.D5, R7.Pin_0
  N6: Arduino1.D4, R6.Pin_0
  N7: Arduino1.D3, R5.Pin_0
  N8: Arduino1.D2, R4.Pin_0
  N9: Arduino1.+5V, R3.wiper
  N10: Arduino1.GND, LED2.blue_anode, C1.+, LED3.common_cathode, MIC1.pin1, LED4.blue_anode, IC1.pin1, IC1.pin2, IC1.pin3, IC1.pin4
  N11: Arduino1.A1, IC1.pin8
  N12: Arduino1.A2, IC1.pin7
  N13: Arduino1.A3, IC1.pin6
  N14: Arduino1.A4, IC1.pin5
  N15: LED1.common_cathode, R9.Pin_1
  N16: LED2.common_cathode, R7.Pin_1
  N17: LED2.green_anode, R6.Pin_1
  N18: R3.leg1, MIC1.pin2
  N19: R4.Pin_1, LED3.blue_anode
  N20: R5.Pin_1, LED3.red_anode
  N21: R10.Pin_1, LED4.green_anode
  N22: R11.Pin_1, LED4.common_cathode
